# Fritzing sketch 1_24207911863 (saved by Fritzing 1.0.5)
breadboards: 1

parts:
  Part1 = Arduino Uno (Rev3)
  8x8_LED_Modul_mit_MAX1 = 8x8 LED Modul mit MAX7219 [package=THT]

nets:
  N1: Part1.D5_PWM, 8x8_LED_Modul_mit_MAX1.CS_Eingang
  N2: Part1.D6_PWM, 8x8_LED_Modul_mit_MAX1.CLK_Eingang
  N3: Part1.D7, 8x8_LED_Modul_mit_MAX1.DIN_Eingang
  N4: Part1.5V, 8x8_LED_Modul_mit_MAX1.VCC_Eingang
  N5: Part1.GND, 8x8_LED_Modul_mit_MAX1.GND_Eingang
